# Fritzing sketch прототип1 (saved by Fritzing 0.9.3b)
breadboards: 1

parts:
  Disp1 = LBT2088AH [part_number=LBT2088AH]
  Часть1 = Arduino Uno (Rev3)
  VCC1 = Battery
  Часть2 = Adafruit MAX9814 Electret Microphone Amplifier [part_number="Adafruit #1713"]
  S1 = Toggle Switch [package=THT]
  R1 = Resistor [tolerance=±5% resistance=220 package=THT]
  LED1 = LED - 5mm [color="Red (633nm)" package="5 mm [THT]"]

nets:
  VIN: Disp1.pin_10, Часть1.VIN, VCC1.+, Часть2.VDD
  GND: Disp1.pin_11, Часть1.GND, Часть2.GND, S1.L1, LED1.cathode
  N1: Disp1.pin_14, Часть1.D4
  N2: Часть1.D2, R1.Pin_1
  N3: Часть1.D3_PWM, Часть2.OUTPUT
  N4: VCC1.-, S1.L2
  N5: R1.Pin_0, LED1.anode

custom parts:
  Adafruit MAX9814 Electret Microphone Amplifier: Add an ear to your project with this well-designed electret microphone amplifier with AGC. This fully assembled and tested board comes with a 20-20KHz electret microphone soldered on. For the amplification, we use the Maxim MAX9814, a specialty chip that is designed for amplifying electret microphones in situations where the loudness of the audio isn't predictable. This fancy microphone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
